# Fritzing sketch electronics (saved by Fritzing 0.9.2b)
breadboards: 1

parts:
  NEMA_23 = Stepper Motor - Unipolar [part_number="SOYO SY57STH56-1006A"]  # not connected
  DRV8825 = SO16 [chip_label=DRV8825 part_number=#2133 package=SO]  # not connected
  C1 = Electrolytic Capacitor [capacitance=0.1mF package="100 mil [THT, electrolytic]"]  # not connected
  Power_plug1 = Power plug  # not connected
  JP1 = Header 12 [package=1x12_machine-pin-header_lock.004]
  Bauteil1 = Arduino Uno (Rev3)
  RE1 = Rotary Encoder [package=THT]  # not connected

nets:
  N1: JP1.6, Bauteil1.D5_PWM
  N2: JP1.7, Bauteil1.D6_PWM
  N3: JP1.8, Bauteil1.D7
  N4: JP1.11, Bauteil1.GND
  N5: JP1.12, Bauteil1.5V

notes:
  A = Black -> 1A
  o1 = Yellow
  C = Green -> 1B
  D = Blue -> 2B
  o2 = While
  B = Red -> 2A
  Signal A -> green
  Signal B -> yellow
  Signal B- -> black
  Signal A- -> blue
  Signal Z -> gray
  Signal Z- -> pink
  VCC -> brown
  Grnd -> white
  caseing -> white-blue
